// Logisim project sagui.circ as structural Verilog: 5 circuits, main circuit main
module main (
);

  wire Clk, JorB, not_1_out, RamOutput, RamWrite, RegWrite, switch_1_p2, switch_2_p2, switch_3_p2, WbOp;
  wire [1:0] PcOp;
  wire [2:0] AluOp;
  wire [7:0] adder_1_out, adder_2_out, banco_reg_1_readdata1, banco_reg_1_readdata2, Imm, Instrucoes_data,
       multiplexer_1_out, multiplexer_2_out, PC_q, ram_1_dout, switch_1_p3;

  Clock clock_1 (.out(Clk));
  Register PC (.D(multiplexer_1_out), .en(1'b1), .clk(Clk), .Q(PC_q));  // open: clr
  ROM Instrucoes (.addr(PC_q), .data(Instrucoes_data));
  Adder adder_1 (.a(PC_q), .b(8'h4), .out(adder_1_out));  // open: cin, cout
  // Probe on Instrucoes_data
  Adder adder_2 (.a(PC_q), .b(Imm), .out(adder_2_out));  // open: cin, cout
  // Probe on Instrucoes_data[3:2]
  assign Imm = {{4{Instrucoes_data[3]}}, Instrucoes_data[3:0]};  // Bit_Extender bit_extender_1
  Multiplexer #(.select(2), .width(8)) multiplexer_1 (
    .in0(adder_1_out), .in1(banco_reg_1_readdata2), .in2(adder_2_out), .out(multiplexer_1_out), .sel(2'b00));  // open: in3
  Ctrl ctrl_1 (
    .Opcode(Instrucoes_data[7:4]), .RegWrite(RegWrite), .RamWrite(RamWrite), .OutputRam(RamOutput),
    .WbOp(WbOp), .AluOp(AluOp), .PcOp(PcOp), .JorB(JorB));
  Multiplexer #(.width(8)) multiplexer_2 (
    .in0(switch_1_p3), .in1(ram_1_dout), .out(multiplexer_2_out), .sel(switch_1_p2));
  // Switch switch_1: pin names not known; wires that end beside it: 1'b1, switch_1_p2, switch_1_p3
  banco_reg banco_reg_1 (
    .Clk(Clk), .WriteRegister(Instrucoes_data[3:2]), .WriteData(multiplexer_2_out), .RegWrite(not_1_out),
    .ReadRegister1(Instrucoes_data[3:2]), .ReadRegister2(Instrucoes_data[1:0]),
    .ReadData2(banco_reg_1_readdata2), .ReadData1(banco_reg_1_readdata1));
  // Probe on banco_reg_1_readdata1
  not not_1 (not_1_out, switch_3_p2);
  ALU alu_1 (
    .Operand1(banco_reg_1_readdata1), .Operand2(banco_reg_1_readdata2), .ALUOp(AluOp), .Result(switch_1_p3));  // open: Zero
  // Probe on switch_1_p3
  // Switch switch_2: pin names not known; wires that end beside it: 1'b1, switch_2_p2
  // Switch switch_3: pin names not known; wires that end beside it: 1'b1, switch_3_p2
  RAM ram_1 (
    .addr(banco_reg_1_readdata2), .we(switch_3_p2), .oe(switch_2_p2), .clk(Clk), .din(banco_reg_1_readdata1),
    .dout(ram_1_dout));
  // Probe on ram_1_dout

  // Notes on the sheet:
  //   pc + imm
  //   pc + 4
  //   Opcode
  //   Reg ou Imm
  //   Ra
  //   Rb
  //   pc = rb
endmodule

module banco_reg (
  input  Clk,
  input  [1:0] ReadRegister1,
  input  [7:0] WriteData,
  input  [1:0] ReadRegister2,
  input  [1:0] WriteRegister,
  input  RegWrite,
  output [7:0] ReadData1,
  output [7:0] ReadData2
);

  wire demultiplexer_2_out0, demultiplexer_2_out1, demultiplexer_2_out2, demultiplexer_2_out3;
  wire [7:0] demultiplexer_1_out0, demultiplexer_1_out1, demultiplexer_1_out2, demultiplexer_1_out3,
       register_1_q, register_2_q, register_3_q, register_4_q;

  Demultiplexer #(.select(2), .width(8)) demultiplexer_1 (
    .out0(demultiplexer_1_out0), .out1(demultiplexer_1_out1), .out2(demultiplexer_1_out2),
    .out3(demultiplexer_1_out3), .in(WriteData), .sel(WriteRegister));
  Demultiplexer #(.select(2)) demultiplexer_2 (
    .out0(demultiplexer_2_out0), .out1(demultiplexer_2_out1), .out2(demultiplexer_2_out2),
    .out3(demultiplexer_2_out3), .in(RegWrite), .sel(WriteRegister));
  Register register_1 (.D(demultiplexer_1_out0), .en(demultiplexer_2_out0), .clk(Clk), .Q(register_1_q));  // open: clr
  Register register_2 (.D(demultiplexer_1_out1), .en(demultiplexer_2_out1), .clk(Clk), .Q(register_2_q));  // open: clr
  Register register_3 (.D(demultiplexer_1_out2), .en(demultiplexer_2_out2), .clk(Clk), .Q(register_3_q));  // open: clr
  Register register_4 (.D(demultiplexer_1_out3), .en(demultiplexer_2_out3), .clk(Clk), .Q(register_4_q));  // open: clr
  Multiplexer #(.select(2), .width(8)) multiplexer_1 (
    .in0(register_1_q), .in1(register_2_q), .in2(register_3_q), .in3(register_4_q), .out(ReadData1),
    .sel(ReadRegister1));
  Multiplexer #(.select(2), .width(8)) multiplexer_2 (
    .in0(register_1_q), .in1(register_2_q), .in2(register_3_q), .in3(register_4_q), .out(ReadData2),
    .sel(ReadRegister2));
endmodule

module ALU (
  input  [7:0] Operand1,
  input  [7:0] Operand2,
  input  [2:0] ALUOp,
  output Zero,
  output [7:0] Result
);

  wire [7:0] adder_1_out, and_1_out, not_1_out, or_1_out, shifter_1_out, shifter_2_out, subtractor_1_out;

  Adder adder_1 (.a(Operand1), .b(Operand2), .out(adder_1_out));  // open: cin, cout
  Subtractor subtractor_1 (.a(Operand1), .b(Operand2), .out(subtractor_1_out));  // open: bin, bout
  assign and_1_out = Operand1 & Operand2;  // AND_Gate and_1, 8 bits wide
  assign or_1_out = Operand1 | Operand2;  // OR_Gate or_1, 8 bits wide
  assign not_1_out = ~Operand1;  // NOT_Gate not_1, 8 bits wide
  Shifter shifter_1 (.in(Operand1), .\dist (Operand2[2:0]), .out(shifter_1_out));
  Shifter #(.shift("lr")) shifter_2 (.in(Operand1), .\dist (Operand2[2:0]), .out(shifter_2_out));
  Multiplexer #(.select(3), .width(8)) multiplexer_1 (
    .in1(adder_1_out), .in2(subtractor_1_out), .in3(and_1_out), .in4(or_1_out), .in5(not_1_out),
    .in6(shifter_1_out), .in7(shifter_2_out), .out(Result), .sel(ALUOp));  // open: in0
  IsZero iszero_1 (.Value(Result), .Result(Zero));
endmodule

module IsZero (
  input  [7:0] Value,
  output Result
);

  and and_1 (Result, 1'b1, ~Value[0], ~Value[1], ~Value[2], ~Value[3], ~Value[4], ~Value[5], ~Value[6], ~Value[7]);  // AND_Gate
endmodule

module Ctrl (
  input  [3:0] Opcode,
  output RegWrite,
  output RamWrite,
  output OutputRam,
  output WbOp,
  output [2:0] AluOp,
  output [1:0] PcOp,
  output JorB
);

  wire and_1_out, and_2_out, and_4_out, and_5_out, and_6_out, and_7_out, not_2_out, not_4_out;

  not not_1 (WbOp, Opcode[3]);
  not not_2 (not_2_out, Opcode[2]);
  not not_3 (JorB, Opcode[1]);
  not not_4 (not_4_out, Opcode[0]);
  and and_1 (and_1_out, Opcode[2], not_4_out);
  and and_2 (and_2_out, Opcode[2], Opcode[1]);
  and and_3 (RamWrite, WbOp, Opcode[2], JorB, Opcode[0]);
  and and_4 (and_4_out, Opcode[2], Opcode[0]);
  and and_5 (and_5_out, Opcode[2], Opcode[1]);
  and and_6 (and_6_out, Opcode[1], Opcode[0]);
  and and_7 (and_7_out, Opcode[3], JorB, not_4_out);
  and and_8 (AluOp[0], Opcode[3], not_4_out);
  and and_9 (PcOp[1], WbOp, not_2_out, not_4_out);
  and and_10 (PcOp[0], WbOp, not_2_out, Opcode[0]);
  or or_1 (RegWrite, and_1_out, and_2_out, Opcode[3]);
  or or_2 (AluOp[2], WbOp, and_4_out, and_5_out);
  or or_3 (AluOp[1], and_6_out, and_7_out);

  assign OutputRam = 1'b1;
endmodule
